// Logisim project alu.circ as structural Verilog: 1 circuit, main circuit alu
module alu (
  input  [31:0] A,
  input  [31:0] B,
  input  [3:0] ALUSel,
  output [31:0] Result
);

  wire comparator_1_lt;
  wire [4:0] bit_extender_1_out, bit_extender_2_out, bit_extender_3_out;
  wire [5:0] bitadder_1_out, bitadder_2_out;
  wire [31:0] add, and_result, bit_extender_5_out, bit_extender_6_out, cnto_result, divu_result, mulh_result,
       mulhu_result, mult_result, or_result, remu_result, sll_result, slt_result, sra_result, srl_result,
       sub_result, xor_result;

  Bit_Extender #(.in_width(32), .out_width(5)) bit_extender_1 (.in(B), .out(bit_extender_1_out));
  Bit_Extender #(.in_width(32), .out_width(5)) bit_extender_2 (.in(B), .out(bit_extender_2_out));
  Bit_Extender #(.in_width(32), .out_width(5)) bit_extender_3 (.in(B), .out(bit_extender_3_out));
  Adder #(.width(32)) adder_1 (.a(A), .b(B), .out(add));  // open: cin, cout
  assign and_result = A & B;  // AND_Gate and_1, 32 bits wide
  assign or_result = A | B;  // OR_Gate or_1, 32 bits wide
  assign xor_result = A ^ B;  // XOR_Gate xor_1, 32 bits wide
  Shifter #(.width(32), .shift("lr")) shifter_1 (.in(A), .\dist (bit_extender_1_out), .out(srl_result));
  Shifter #(.width(32), .shift("ar")) shifter_2 (.in(A), .\dist (bit_extender_2_out), .out(sra_result));
  Shifter #(.width(32)) shifter_3 (.in(A), .\dist (bit_extender_3_out), .out(sll_result));
  Comparator #(.width(32)) comparator_1 (.a(A), .b(B), .lt(comparator_1_lt));  // open: gt, eq
  assign slt_result = {{31{1'b0}}, comparator_1_lt};  // Bit_Extender bit_extender_4
  // Probe on A
  // Probe on B
  Divider #(.width(32)) divider_1 (.a(A), .b(B), .out(divu_result));  // open: upper, rem
  Divider #(.width(32)) divider_2 (.a(A), .b(B), .rem(remu_result));  // open: out, upper
  Multiplier #(.width(32)) multiplier_1 (.a(A), .b(B), .out(mult_result));  // open: cin, cout
  Multiplier #(.width(32)) multiplier_2 (.a(A), .b(B), .cout(mulhu_result));  // open: out, cin
  Subtractor #(.width(32)) subtractor_1 (.a(A), .b(B), .out(sub_result));  // open: bin, bout
  BitAdder #(.width(32)) bitadder_1 (.in0(A), .out(bitadder_1_out));
  BitAdder #(.width(32)) bitadder_2 (.in0(B), .out(bitadder_2_out));
  Multiplier #(.width(32)) multiplier_3 (.a(A), .b(B), .out(mulh_result));  // open: cin, cout
  // Probe on mulhu_result
  assign bit_extender_5_out = {{26{1'b0}}, bitadder_1_out};  // Bit_Extender bit_extender_5
  assign bit_extender_6_out = {{26{1'b0}}, bitadder_2_out};  // Bit_Extender bit_extender_6
  Adder #(.width(32)) adder_2 (.a(bit_extender_5_out), .b(bit_extender_6_out), .out(cnto_result));  // open: cin, cout
  Multiplexer #(.select(4), .width(32), .enable("false")) multiplexer_1 (
    .in0(add), .in1(and_result), .in2(or_result), .in3(xor_result), .in4(srl_result), .in5(sra_result),
    .in6(sll_result), .in7(slt_result), .in8(divu_result), .in9(remu_result), .in10(mult_result),
    .in11(mulhu_result), .in12(sub_result), .in13(cnto_result), .in14(mulh_result), .out(Result), .sel(ALUSel));  // open: in15

  // Notes on the sheet:
  //   INPUTS to your circuit
  //   DON'T CHANGE THE LOCATIONS OF THE INPUTS AND OUTPUTS!
  //   OUTPUT from your circuit
endmodule
