// Logisim project alu.circ as structural Verilog: 1 circuit, main circuit alu
module alu (
  input  [31:0] A,
  input  [31:0] B,
  input  [3:0] ALUSel,
  output [31:0] Result
);

  wire comparator_1_lt, if_carry_in, sign;
  wire [4:0] bit_extender_1_out, bit_extender_2_out, bit_extender_3_out;
  wire [5:0] bitadder_1_out, bitadder_2_out;
  wire [31:0] add, and_result, bit_extender_5_out, bit_extender_6_out, cnto_result, divu_result, mulh_result,
       mulhu_result, mult_result, multiplexer_1_out, multiplexer_2_out, multiplexer_3_out, multiplier_3_cout,
       multiplier_3_out, negator_1_out, negator_2_out, negator_3_out, or_result, remu_result, sll_result,
       slt_result, sra_result, srl_result, sub_result, subtractor_2_out, xor_result;

  Bit_Extender #(.in_width(32), .out_width(5)) bit_extender_1 (.in(B), .out(bit_extender_1_out));
  Bit_Extender #(.in_width(32), .out_width(5)) bit_extender_2 (.in(B), .out(bit_extender_2_out));
  Bit_Extender #(.in_width(32), .out_width(5)) bit_extender_3 (.in(B), .out(bit_extender_3_out));
  Adder #(.width(32)) adder_1 (.a(A), .b(B), .out(add));  // open: cin, cout
  assign and_result = A & B;  // AND_Gate and_1, 32 bits wide
  assign or_result = A | B;  // OR_Gate or_1, 32 bits wide
  assign xor_result = A ^ B;  // XOR_Gate xor_1, 32 bits wide
  Shifter #(.width(32), .shift("lr")) shifter_1 (.in(A), .\dist (bit_extender_1_out), .out(srl_result));
  Shifter #(.width(32), .shift("ar")) shifter_2 (.in(A), .\dist (bit_extender_2_out), .out(sra_result));
  Shifter #(.width(32)) shifter_3 (.in(A), .\dist (bit_extender_3_out), .out(sll_result));
  Comparator #(.width(32)) comparator_1 (.a(A), .b(B), .lt(comparator_1_lt));  // open: gt, eq
  assign slt_result = {{31{1'b0}}, comparator_1_lt};  // Bit_Extender bit_extender_4
  Divider #(.width(32)) divider_1 (.a(A), .b(B), .out(divu_result));  // open: upper, rem
  Divider #(.width(32)) divider_2 (.a(A), .b(B), .rem(remu_result));  // open: out, upper
  Multiplier #(.width(32)) multiplier_1 (.a(A), .b(B), .out(mult_result));  // open: cin, cout
  Multiplier #(.width(32)) multiplier_2 (.a(A), .b(B), .cout(mulhu_result));  // open: out, cin
  Subtractor #(.width(32)) subtractor_1 (.a(A), .b(B), .out(sub_result));  // open: bin, bout
  BitAdder #(.width(32)) bitadder_1 (.in0(A), .out(bitadder_1_out));
  BitAdder #(.width(32)) bitadder_2 (.in0(B), .out(bitadder_2_out));
  Negator #(.width(32)) negator_1 (.in(A), .out(negator_1_out));
  Negator #(.width(32)) negator_2 (.in(B), .out(negator_2_out));
  assign bit_extender_5_out = {{26{1'b0}}, bitadder_1_out};  // Bit_Extender bit_extender_5
  assign bit_extender_6_out = {{26{1'b0}}, bitadder_2_out};  // Bit_Extender bit_extender_6
  Multiplexer #(.width(32), .enable("false")) multiplexer_1 (
    .in0(A), .in1(negator_1_out), .out(multiplexer_1_out), .sel(A[31]));
  Multiplexer #(.width(32), .enable("false")) multiplexer_2 (
    .in0(B), .in1(negator_2_out), .out(multiplexer_2_out), .sel(B[31]));
  xor xor_2 (sign, A[31], B[31]);
  Adder #(.width(32)) adder_2 (.a(bit_extender_5_out), .b(bit_extender_6_out), .out(cnto_result));  // open: cin, cout
  Multiplier #(.width(32)) multiplier_3 (
    .a(multiplexer_1_out), .b(multiplexer_2_out), .out(multiplier_3_out), .cout(multiplier_3_cout));  // open: cin
  Negator #(.width(32)) negator_3 (.in(multiplier_3_cout), .out(negator_3_out));
  Comparator #(.width(32)) comparator_2 (.a(multiplier_3_out), .b({32{1'b0}}), .eq(if_carry_in));  // open: gt, lt
  Subtractor #(.width(32)) subtractor_2 (.a(negator_3_out), .b(32'h1), .out(subtractor_2_out));  // open: bin, bout
  Multiplexer #(.width(32), .enable("false")) multiplexer_3 (
    .in0(subtractor_2_out), .in1(negator_3_out), .out(multiplexer_3_out), .sel(if_carry_in));
  Multiplexer #(.select(4), .width(32), .enable("false")) multiplexer_4 (
    .in0(add), .in1(and_result), .in2(or_result), .in3(xor_result), .in4(srl_result), .in5(sra_result),
    .in6(sll_result), .in7(slt_result), .in8(divu_result), .in9(remu_result), .in10(mult_result),
    .in11(mulhu_result), .in12(sub_result), .in13(cnto_result), .in14(mulh_result), .out(Result), .sel(ALUSel));  // open: in15
  Multiplexer #(.width(32), .enable("false")) multiplexer_5 (
    .in0(multiplier_3_cout), .in1(multiplexer_3_out), .out(mulh_result), .sel(sign));

  // Other names for the same wires on the sheet: sign_A = A[31]; sign_B = B[31]

  // Notes on the sheet:
  //   INPUTS to your circuit
  //   DON'T CHANGE THE LOCATIONS OF THE INPUTS AND OUTPUTS!
  //   OUTPUT from your circuit
endmodule
